// Digital circuit 4-bit_ALU_embedded.dig as structural Verilog
module _4_bit_ALU_embedded (
  input  [3:0] A,
  input  [3:0] B,
  input  [2:0] Sel__Cin,
  output [3:0] Sum,
  output C_out
);

  wire [3:0] multiplexer_1_out, not_1_out, not_2_out;

  assign not_1_out = ~B;  // Not not_1, 4 bits wide
  assign not_2_out = ~4'b0000;  // Not not_2, 4 bits wide
  Multiplexer #(.Selector_Bits(2), .Bits(4)) multiplexer_1 (
    .sel(Sel__Cin[2:1]), .in_0(B), .in_1(not_1_out), .in_2(4'b0000), .in_3(not_2_out), .out(multiplexer_1_out));
  _4_bit_adder _4_bit_adder_1 (.A(A), .B(multiplexer_1_out), .Cin(Sel__Cin[0]), .S(Sum), .Cout(C_out));
  // Pins of 2 and 3 bits meet at Sel__Cin
endmodule
