// Digital circuit 4-bit_adder.dig as structural Verilog
module _4_bit_adder (
  input  [3:0] A,
  input  [3:0] B,
  input  Cin,
  output [3:0] S,
  output Cout
);

  wire hw1_1bit_full_adder_1_cout, hw1_1bit_full_adder_2_cout, hw1_1bit_full_adder_3_cout;

  HW1_1Bit_Full_Adder hw1_1bit_full_adder_1 (
    .A(A[0]), .B(B[0]), .Cin(Cin), .SUM(S[0]), .Cout(hw1_1bit_full_adder_1_cout));
  HW1_1Bit_Full_Adder hw1_1bit_full_adder_2 (
    .A(A[1]), .B(B[1]), .Cin(hw1_1bit_full_adder_1_cout), .SUM(S[1]), .Cout(hw1_1bit_full_adder_2_cout));
  HW1_1Bit_Full_Adder hw1_1bit_full_adder_3 (
    .A(A[2]), .B(B[2]), .Cin(hw1_1bit_full_adder_2_cout), .SUM(S[2]), .Cout(hw1_1bit_full_adder_3_cout));
  HW1_1Bit_Full_Adder hw1_1bit_full_adder_4 (
    .A(A[3]), .B(B[3]), .Cin(hw1_1bit_full_adder_3_cout), .SUM(S[3]), .Cout(Cout));
endmodule
