// Digital circuit CPU4bit.dig as structural Verilog
module CPU4bit (
  input  [3:0] InstructionMemory_dataInput,
  input  [1:0] InstructionMemory_ctrl,
  input  clk,
  input  [3:0] Dummy,
  output [1:0] IR_HI_1_0,
  output [1:0] IR_HI_3_2,
  output [1:0] IR_LO_1_0,
  output [1:0] IR_LO_3_2,
  output [4:0] state,
  output IR_HI_Write,
  output IR_LO_Write,
  output PC_inc,
  output [3:0] IP,
  output [3:0] Mem_dataout,
  output [3:0] ALU_out,
  output ALU_src
);

  wire control_rtype_1_writeback, not_2_out, xor_1_out;
  wire [1:0] multiplexer_1_out, multiplexer_2_out, multiplexer_3_out, multiplexer_6_out, not_1_out;
  wire [2:0] and_1_out;
  wire [3:0] demultiplexer_1_out_0, demultiplexer_1_out_1, InstructionMemory_data_output, multiplexer_7_out,
       multiplexer_8_out, register_file_1_read_data_1, register_file_1_read_data_2;
  wire [7:0] multiplexer_4_out, multiplexer_5_out;

  Multiplexer #(.Bits(2)) multiplexer_1 (.sel(PC_inc), .in_0(2'b10), .in_1(2'b11), .out(multiplexer_1_out));
  program_counter program_counter_1 (
    .Input(4'b0000), .clk(clk), .Clear_Store_Load_Increment(multiplexer_1_out), ._1(4'b0001), .Output(IP));
  DRAM InstructionMemory (
    .Address_bits(IP), .Clk(clk), .clear_store_load(InstructionMemory_ctrl),
    .Data_Input(InstructionMemory_dataInput), .Data_Output(InstructionMemory_data_output));
  Demultiplexer #(.Bits(4)) demultiplexer_1 (
    .sel(IP[0]), .in(InstructionMemory_data_output), .out_0(demultiplexer_1_out_0),
    .out_1(demultiplexer_1_out_1));
  Multiplexer #(.Bits(2)) multiplexer_2 (.sel(IR_LO_Write), .in_0(2'b10), .in_1(2'b01), .out(multiplexer_2_out));
  Multiplexer #(.Bits(2)) multiplexer_3 (.sel(IR_HI_Write), .in_0(2'b10), .in_1(2'b01), .out(multiplexer_3_out));
  general_purpose_register Instruction_Register__HI (
    .Input(demultiplexer_1_out_0), .clk(clk), .Clear_Store_Load(multiplexer_3_out),
    .Output({IR_HI_3_2, IR_HI_1_0}));
  general_purpose_register Instruction_Register__LO (
    .Input(demultiplexer_1_out_1), .clk(clk), .Clear_Store_Load(multiplexer_2_out),
    .Output({IR_LO_3_2, IR_LO_1_0}));
  control_RType control_rtype_1 (
    .clk(clk), .State(state), .IR_HI_write(IR_HI_Write), .IR_LO_Write(IR_LO_Write),
    .WriteBack(control_rtype_1_writeback), .PC_Inc(PC_inc));
  assign not_1_out = ~IR_HI_3_2;  // Not not_1, 2 bits wide
  not not_2 (not_2_out, IR_LO_1_0[1]);
  xor xor_1 (xor_1_out, IR_LO_1_0[1], IR_LO_1_0[0]);
  and and_1 (and_1_out[0], IR_LO_1_0[0], IR_LO_1_0[1], not_1_out[0], not_1_out[1]);
  and and_2 (and_1_out[1], not_1_out[1], not_1_out[0], IR_LO_1_0[0], not_2_out);
  Multiplexer #(.Selector_Bits(2), .Bits(8)) multiplexer_4 (
    .sel(IR_HI_1_0), .in_0(8'ha9), .in_1(8'ha6), .in_2(8'h9a), .in_3(8'h6a), .out(multiplexer_4_out));
  and and_3 (and_1_out[2], xor_1_out, not_1_out[0], not_1_out[1]);
  and and_4 (ALU_src, IR_HI_3_2[0], IR_HI_3_2[1]);
  Multiplexer #(.Bits(8)) multiplexer_5 (
    .sel(control_rtype_1_writeback), .in_0(8'haa), .in_1(multiplexer_4_out), .out(multiplexer_5_out));
  Multiplexer #(.Bits(2)) multiplexer_6 (.sel(IR_HI_1_0[0]), .in_0(2'b10), .in_1(2'b01), .out(multiplexer_6_out));
  register_file register_file_1 (
    .Control(multiplexer_5_out), .Write_Reg(IR_HI_1_0), .Read_Reg_2(IR_LO_3_2), .Read_Reg_1(IR_HI_1_0),
    .clk(clk), .Write_data(multiplexer_8_out), .Read_Data_1(register_file_1_read_data_1),
    .Read_Data_2(register_file_1_read_data_2));
  Multiplexer #(.Bits(4)) multiplexer_7 (
    .sel(ALU_src), .in_0(register_file_1_read_data_2), .in_1({IR_LO_3_2, IR_LO_1_0}), .out(multiplexer_7_out));
  // _4_bit_ALU_embedded _4_bit_alu_embedded_1: pin names not known; wires that end beside it: register_file_1_read_data_1, multiplexer_7_out, and_1_out, ALU_out
  DRAM dram_1 (
    .Address_bits({2'b00, IR_LO_3_2}), .Clk(clk), .clear_store_load(multiplexer_6_out),
    .Data_Input(register_file_1_read_data_1), .Data_Output(Mem_dataout));
  Multiplexer #(.Selector_Bits(2), .Bits(4)) multiplexer_8 (
    .sel(IR_HI_3_2), .in_0(ALU_out), .in_1(Mem_dataout), .in_2({IR_LO_3_2, IR_LO_1_0}), .in_3(Dummy),
    .out(multiplexer_8_out));
endmodule

/* Test case:
# --- Test: program Instruction Memory via buses and run a small program ---
# Program:
#   0/1 : LDI R1,#5   (HI=9,  LO=5)
#   2/3 : LDI R2,#3   (HI=10, LO=3)
#   4/5 : ADD R2,R1   (HI=2,  LO=4)  ; ALU_out should be 8 during execute
#   6/7 : SUB R2,R1   (HI=2,  LO=5)  ; ALU_out should be 3 during execute

clk state PC_inc IP InstructionMemory_dataInput InstructionMemory_ctrl IR-HI-Write IR-LO-Write IR_HI[3:2] IR_HI[1:0] IR_LO[3:2] IR_LO[1:0] ALU_out

# =========================================================
# 1. PROGRAM INSTRUCTION MEMORY USING NORMAL INTERFACE
# ---------------------------------------------------------
# We rely on your control unit / PC_inc to step through IF1/IF2,
# and we just provide the data nibble and InstructionMemory_ctrl
# to store HI/LO nibbles at successive addresses.
#
# Addresses and nibbles:
#   addr 0 : 0x9  (HI of LDI R1,#5)
#   addr 1 : 0x5  (LO of LDI R1,#5)
#   addr 2 : 0xA  (HI of LDI R2,#3)
#   addr 3 : 0x3  (LO of LDI R2,#3)
#   addr 4 : 0x2  (HI of ADD R2,R1)
#   addr 5 : 0x4  (LO of ADD R2,R1)
#   addr 6 : 0x2  (HI of SUB R2,R1)
#   addr 7 : 0x5  (LO of SUB R2,R1)
# =========================================================

# Spin FSM / PC into a stable starting state (as you were doing before)
repeat(39) C X X X 0 0 X X X X X X X

# --- FIRST instruction: LDI R1,#5 ---
# addr 0 <- 0x9  (HI of LDI R1,#5)
C X X X 9 1 X X  X X X X X
# addr 1 <- 0x5  (LO of LDI R1,#5)
C X X X 5 1 X X  X X X X X
# next three cycles: decode, execute, writeback – ALU_out don't-care
repeat(3) C X X X 0 0 X X X X X X X

# --- SECOND instruction: LDI R2,#3 ---
# addr 2 <- 0xA  (HI of LDI R2,#3)
C X X X 10 1 X X  X X X X X
# addr 3 <- 0x3  (LO of LDI R2,#3)
C X X X 3  1 X X  X X X X X
# next three cycles: decode, execute, writeback – ALU_out don't-care
repeat(3) C X X X 0 0 X X X X X X X

# --- THIRD instruction: ADD R2,R1 ---
# addr 4 <- 0x2  (HI of ADD R2,R1)
C X X X 2 1 X X  X X X X X
# addr 5 <- 0x4  (LO of ADD R2,R1)
C X X X 4 1 X X  X X X X X
# next three cycles: decode, execute, writeback
# During the EXECUTE cycle of this ADD, ALU_out[3:0] should be 8 (0x8).
# Once you know which 'state' bit = Execute, you can change the Xs
# on the correct cycle to (8) instead of X.
repeat(3) C X X X 0 0 X X X X X X X

# --- FOURTH instruction: SUB R2,R1 ---
# addr 6 <- 0x2  (HI of SUB R2,R1)
C X X X 2 1 X X  X X X X X
# addr 7 <- 0x5  (LO of SUB R2,R1)
C X X X 5 1 X X  X X X X X
# next three cycles: decode, execute, writeback
# During the EXECUTE cycle of this SUB, ALU_out[3:0] should be 3 (0x3).
# Again, once you align this with 'state', you can set ALU_out to 3
# on the right cycle.
repeat(3) C X X X 0 0 X X X X X X X

# =========================================================
# 2. RUN / OBSERVE PHASE (OPTIONAL)
# ---------------------------------------------------------
# At this point, the program is in instruction memory and the CPU
# has already stepped through the IF/ID/EX/WB cycles used during
# programming. If you simply keep clocking, you can watch:
#   - R1 being loaded with 5
#   - R2 being loaded with 3
#   - ADD R2,R1 being executed (ALU_out = 8)
#   - SUB R2,R1 being executed (ALU_out = 3)
#
# Because the exact timing of your FSM may differ, we keep ALU_out
# as don't-care here. Once you know *which* cycle is the execute
# stage for ADD and SUB, you can replace the 'X' in ALU_out with
# 8 and 3 at the appropriate lines.
# ==========================================================

# Example: just keep clocking to let the CPU run
repeat(20) C X X X 0 2 X X X X X X X
*/
