// Digital circuit control_RType.dig as structural Verilog
module control_RType (
  input  clk,
  output [4:0] State,
  output IR_HI_write,
  output IR_LO_Write,
  output WriteBack,
  output PC_Inc
);

  D_FF #(.Default(1)) IF1 (.D(State[4]), .C(clk), .Q(IR_HI_write));  // open: nQ
  D_FF IF2 (.D(IR_HI_write), .C(clk), .Q(IR_LO_Write));  // open: nQ
  D_FF Decode (.D(IR_LO_Write), .C(clk), .Q(State[2]));  // open: nQ
  D_FF Execute (.D(State[2]), .C(clk), .Q(State[3]));  // open: nQ
  D_FF u_WriteBack (.D(State[3]), .C(clk), .Q(State[4]));  // open: nQ
  or or_1 (PC_Inc, IR_HI_write, State[4]);

  assign State[1:0] = {IR_LO_Write, IR_HI_write};
  assign WriteBack = State[4];
endmodule
