// Digital circuit program_counter.dig as structural Verilog
module program_counter (
  input  [3:0] Input,
  input  clk,
  input  [1:0] Clear_Store_Load_Increment,
  input  [3:0] _1,
  output [3:0] Output
);

  wire [3:0] add_1_s, multiplexer_1_out;

  Add #(.Bits(4)) add_1 (.a(Output), .b(_1), .c_i(1'b0), .s(add_1_s));  // open: c_o
  Multiplexer #(.Selector_Bits(2), .Bits(4)) multiplexer_1 (
    .sel(Clear_Store_Load_Increment), .in_0(4'b0000), .in_1(Input), .in_2(Output), .in_3(add_1_s),
    .out(multiplexer_1_out));
  D_FF D_3 (.D(multiplexer_1_out[3]), .C(clk), .Q(Output[3]));  // open: nQ
  D_FF D_2 (.D(multiplexer_1_out[2]), .C(clk), .Q(Output[2]));  // open: nQ
  D_FF D_1 (.D(multiplexer_1_out[1]), .C(clk), .Q(Output[1]));  // open: nQ
  D_FF D_0 (.D(multiplexer_1_out[0]), .C(clk), .Q(Output[0]));  // open: nQ

  // Notes on the sheet:
  //   Clear_Store_Load_Increment: 0 = Clear
  //   1 = Store input
  //   2 = Load
  //   3 = Increment +1
  //   _1: default 1
endmodule
