// Digital circuit register_file.dig as structural Verilog
module register_file (
  input  [7:0] Control,
  input  [1:0] Write_Reg,
  input  [1:0] Read_Reg_2,
  input  [1:0] Read_Reg_1,
  input  clk,
  input  [3:0] Write_data,
  output [3:0] Read_Data_1,
  output [3:0] Read_Data_2
);

  wire [3:0] demultiplexer_1_out_0, demultiplexer_1_out_1, demultiplexer_1_out_2, demultiplexer_1_out_3,
       R_0_output, R_1_output, R_2_output, R_3_output;

  Demultiplexer #(.Bits(4), .Selector_Bits(2)) demultiplexer_1 (
    .sel(Write_Reg), .in(Write_data), .out_0(demultiplexer_1_out_0), .out_1(demultiplexer_1_out_1),
    .out_2(demultiplexer_1_out_2), .out_3(demultiplexer_1_out_3));
  general_purpose_register R_0 (
    .Output(R_0_output), .Input(demultiplexer_1_out_0), .Clear_Store_Load(Control[1:0]), .clk(clk));
  general_purpose_register R_1 (
    .Output(R_1_output), .Input(demultiplexer_1_out_1), .Clear_Store_Load(Control[3:2]), .clk(clk));
  general_purpose_register R_2 (
    .Output(R_2_output), .Input(demultiplexer_1_out_2), .Clear_Store_Load(Control[5:4]), .clk(clk));
  general_purpose_register R_3 (
    .Output(R_3_output), .Input(demultiplexer_1_out_3), .Clear_Store_Load(Control[7:6]), .clk(clk));
  Multiplexer #(.Selector_Bits(2), .Bits(4)) multiplexer_1 (
    .sel(Read_Reg_2), .in_0(R_0_output), .in_1(R_1_output), .in_2(R_2_output), .in_3(R_3_output),
    .out(Read_Data_2));
  Multiplexer #(.Bits(4), .Selector_Bits(2)) multiplexer_2 (
    .sel(Read_Reg_1), .in_0(R_0_output), .in_1(R_1_output), .in_2(R_2_output), .in_3(R_3_output),
    .out(Read_Data_1));

  // Notes on the sheet:
  //   Control: Control Signal
endmodule
